# Fritzing sketch DiagramaEsquematico (saved by Fritzing 0.9.10b)
circuit board: 13cm x 7cm
breadboards: 2

parts:
  POWER = YwRobot Breadboard Power Supply [part_number=545043]
  RFID_SENSOR = RFID-RC522-v2
  ESP_WROOM32 = DOIT Esp32 DevKit v1 (30 pins long, 11 pins width) [part_number=ESP32S-PIN30]
  BUZZER = KY-006 Passive Buzzer Module [package="Breakout board"]
  OLED_DISPLAY = 0.91 inch OLED I2C Display 128 x 32 Pixels
  OLED_Display = female pin header, 4 pins [form="♀ (female)"]
  R1 = Resistor [tolerance=±5% resistance=220 package="0603 [SMD]"]
  LED1 = RGB LED (com. anode, rbg) [package="5 mm [THT]"]
  R2 = Resistor [tolerance=±5% resistance=220 package="0603 [SMD]"]
  R3 = Resistor [tolerance=±5% resistance=220 package="0603 [SMD]"]
  R4 = Resistor [tolerance=±5% resistance=220 package="0603 [SMD]"]
  R5 = Resistor [tolerance=±5% resistance=220 package="0603 [SMD]"]
  R6 = Resistor [tolerance=±5% resistance=220 package="0603 [SMD]"]
  LED2 = RGB LED (com. anode, rbg) [package="5 mm [THT]"]

nets:
  3.3V: POWER.VCC#5, RFID_SENSOR.3.3V, OLED_DISPLAY.VCC, OLED_Display.pin2
  N1: POWER.VCC#9, ESP_WROOM32.VIN, LED1.common_anode, LED2.common_anode
  GND: POWER.GND#11, RFID_SENSOR.GND, BUZZER.-, OLED_DISPLAY.GND, OLED_Display.pin1
  N2: POWER.GND#13, ESP_WROOM32.GND
  N3: RFID_SENSOR.SDA, ESP_WROOM32.D5
  N4: RFID_SENSOR.SCK, ESP_WROOM32.D18
  N5: RFID_SENSOR.MOSI, ESP_WROOM32.D23
  N6: RFID_SENSOR.MISO, ESP_WROOM32.D19
  N7: RFID_SENSOR.RST, ESP_WROOM32.D2
  N8: ESP_WROOM32.D21, OLED_DISPLAY.SDA, OLED_Display.pin4
  N9: ESP_WROOM32.D22, OLED_DISPLAY.SCL, OLED_Display.pin3
  N10: ESP_WROOM32.D35, R6.Pin_0
  N11: ESP_WROOM32.D32, R5.Pin_0
  N12: ESP_WROOM32.D33, R4.Pin_0
  N13: ESP_WROOM32.D25, R3.Pin_0
  N14: ESP_WROOM32.D26, R2.Pin_0
  N15: ESP_WROOM32.D27, R1.Pin_0
  N16: ESP_WROOM32.D13, BUZZER.S
  N17: R1.Pin_1, LED1.red_cathode
  N18: LED1.blue_cathode, R2.Pin_1
  N19: LED1.green_cathode, R3.Pin_1
  N20: R4.Pin_1, LED2.red_cathode
  N21: R5.Pin_1, LED2.blue_cathode
  N22: R6.Pin_1, LED2.green_cathode

notes:
  3v
  GND
  SDA
  Produzido por

custom parts:
  YwRobot Breadboard Power Supply: The YwRobot Breadboard Power Supply (MB-V2) has two power rails; they can be 5V or 3V3. Power to the module can be provided through the female USB socket or through the A10 (female) 2.1mm power jack.
  RFID-RC522-v2: A simple China made RFID-RC522 Reader; do check the pin labels, as this is a MFRC522 based clone.
  DOIT Esp32 DevKit v1 (30 pins long, 11 pins width): The DOIT Esp32 DevKit v1 is one of the development board created by DOIT to evaluate the ESP-WROOM-32 module. It is based on the ESP32 microcontroller that boasts Wifi, Bluetooth, Ethernet and Low Power support all in a single chip. (vanepp) made breadboard work, adjusted pin numbering and labels and reduced size of schematic and cleaned up pcb. This chip is 30pins long (2 x15) and 11 pins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
  KY-006 Passive Buzzer Module: Passive Piezoelectric Buzzer Module Keyes KY-006, it can produce a range of sound tones depending on the input frequency.
