# Fritzing sketch frequencia (saved by Fritzing 0.9.10b)
breadboards: 1

parts:
  DISPLAY = Grove OLED 128x96
  RFID_READER = RFID-RC522-v2
  BUZZER = Passive Buzzer
  LED_1 = LEDs [package=led10mm]
  LED_2 = LEDs [package=led10mm]
  R1 = Resistor [tolerance=±5% resistance=470 power=0.25 package=THT]
  R2 = Resistor [tolerance=±5% resistance=330 power=0.25 package=THT]
  5V_Input = Power Jack [package=power_jack_pth_lock]
  ESP32_NodeMCU8266 = ESP32-38PinWide [part_number=ESP32-38PinWide]

nets:
  GND: DISPLAY.GND, RFID_READER.GND, BUZZER.-, LED_1.C, LED_2.C, 5V_Input.GND, ESP32_NodeMCU8266.GND
  VCC: DISPLAY.VCC, RFID_READER.3.3V, ESP32_NodeMCU8266.3.3
  N1: DISPLAY.SDA, ESP32_NodeMCU8266.GPIO22
  N2: DISPLAY.SCL, ESP32_NodeMCU8266.GPIO21
  N3: RFID_READER.SDA, ESP32_NodeMCU8266.GPIO4
  N4: RFID_READER.SCK, ESP32_NodeMCU8266.GPIO18
  N5: RFID_READER.MOSI, ESP32_NodeMCU8266.GPIO17
  N6: RFID_READER.MISO, ESP32_NodeMCU8266.GPIO16
  N7: RFID_READER.RST, ESP32_NodeMCU8266.GPIO5
  N8: BUZZER.S, ESP32_NodeMCU8266.GPIO23
  N9: LED_1.A, R2.Pin_0
  N10: LED_2.A, R1.Pin_0
  N11: R1.Pin_1, ESP32_NodeMCU8266.GPIO33
  N12: R2.Pin_1, ESP32_NodeMCU8266.GPIO32
  N13: 5V_Input.PWR, ESP32_NodeMCU8266.VIN

notes:
  RST
  GND
  3.3v
  MISO
  MOSI
  SCK
  SDA
  +
  SCL
  VCC

custom parts:
  RFID-RC522-v2: A simple China made RFID-RC522 Reader; do check the pin labels, as this is a MFRC522 based clone.
  ESP32-38PinWide: Generic 38-Pin ESP32 with wide format (only access to one side of pins on a breadboard) based on Stephen Lilley's HiLetgo ESP-WROOM-32 ESP32 ESP-32S Development Board.
